// Logisim project control-logic.circ as structural Verilog: 1 circuit, main circuit control_logic
module control_logic (
  input  [31:0] Instruction,
  input  BrEq,
  input  BrLt,
  output PCSel,
  output RegWEn,
  output [2:0] ImmSel,
  output BrUn,
  output ASel,
  output BSel,
  output [3:0] ALUSel,
  output MemWEn,
  output [1:0] WBSel
);

  wire and_1_out, and_2_out, and_3_out, and_4_out, and_5_out, and_6_out, branch_cond, funct3_0, funct3_1,
       funct3_2, funct3_3, funct3_4, funct3_5, funct3_6, funct3_7, funct7_0, funct7_1, funct7_32, g_sig_1,
       g_sig_2, not_1_out, not_2_out, not_3_out, opcode_3, opcode_19, opcode_23, opcode_35, opcode_51,
       opcode_55, opcode_99, opcode_103, opcode_111, s_add, s_addi, s_and, s_andi, s_beq, s_bge, s_bgeu,
       s_blt, s_bltu, s_bne, s_jalr, s_lb, s_lh, s_lw, s_mul, s_mulh, s_mulhu, s_or, s_ori, s_sb, s_sh,
       s_sll, s_slli, s_slt, s_slti, s_sra, s_srai, s_srl, s_srli, s_sub, s_sw, s_xor, s_xori;
  wire [1:0] prio_2;
  wire [4:0] prio_1;
  wire [5:0] adder_1_out, bit_extender_1_out, bit_extender_2_out, ROM_In;
  wire [15:14] rom_1_data;

  ROM #(.addrWidth(6), .dataWidth(16)) rom_1 (
    .addr(ROM_In), .data({rom_1_data, WBSel, MemWEn, ALUSel, BSel, ASel, BrUn, ImmSel, RegWEn}));
  Priority_Encoder #(.select(5)) priority_encoder_1 (
    .in0(s_add), .in1(s_mul), .in2(s_sub), .in3(s_sll), .in4(s_mulh), .in5(s_mulhu), .in6(s_slt),
    .in7(s_xor), .in8(s_srl), .in9(s_sra), .in10(s_or), .in11(s_and), .in12(s_lb), .in13(s_lh), .in14(s_lw),
    .in15(s_addi), .in16(s_slli), .in17(s_slti), .in18(s_xori), .in19(s_srli), .in20(s_srai), .in21(s_ori),
    .in22(s_andi), .in23(s_sb), .in24(s_sh), .in25(s_sw), .in26(s_beq), .in27(s_bne), .in28(s_blt),
    .in29(s_bge), .in30(s_bltu), .in31(s_bgeu), .out(prio_1), .gs(g_sig_1));  // open: en_out, en_in
  Priority_Encoder #(.select(2)) priority_encoder_2 (
    .in0(opcode_23), .in1(opcode_55), .in2(opcode_111), .in3(s_jalr), .out(prio_2), .gs(g_sig_2));  // open: en_out, en_in
  assign bit_extender_1_out = {{4{1'b0}}, prio_2};  // Bit_Extender bit_extender_1
  Adder #(.width(6)) adder_1 (.a(bit_extender_1_out), .b(6'b100000), .out(adder_1_out));  // open: cin, cout
  assign bit_extender_2_out = {{1{1'b0}}, prio_1};  // Bit_Extender bit_extender_2
  Multiplexer #(.enable("false"), .width(6)) multiplexer_1 (
    .in0(adder_1_out), .in1(bit_extender_2_out), .out(ROM_In), .sel(g_sig_1));
  and and_1 (and_1_out, BrEq, s_beq);
  and and_2 (and_2_out, s_bne, not_1_out);
  not not_1 (not_1_out, BrEq);
  and and_3 (and_3_out, s_blt, BrLt);
  and and_4 (and_4_out, s_bge, not_2_out);
  not not_2 (not_2_out, BrLt);
  and and_5 (and_5_out, s_bgeu, not_3_out);
  not not_3 (not_3_out, BrLt);
  and and_6 (and_6_out, s_bltu, BrLt);
  or or_1 (PCSel, branch_cond, opcode_111, s_jalr);
  or or_2 (branch_cond, and_1_out, and_2_out, and_3_out, and_4_out, and_5_out, and_6_out);
  Comparator #(.mode("unsigned"), .width(7)) comparator_1 (
    .a(Instruction[6:0]), .b(7'b0110011), .eq(opcode_51));  // open: gt, lt
  Comparator #(.mode("unsigned"), .width(7)) comparator_2 (
    .a(Instruction[6:0]), .b(7'b0010011), .eq(opcode_19));  // open: gt, lt
  Comparator #(.mode("unsigned"), .width(7)) comparator_3 (
    .a(Instruction[6:0]), .b(7'b0000011), .eq(opcode_3));  // open: gt, lt
  Comparator #(.mode("unsigned"), .width(7)) comparator_4 (
    .a(Instruction[6:0]), .b(7'b0100011), .eq(opcode_35));  // open: gt, lt
  Comparator #(.mode("unsigned"), .width(7)) comparator_5 (
    .a(Instruction[6:0]), .b(7'b1100011), .eq(opcode_99));  // open: gt, lt
  Comparator #(.mode("unsigned"), .width(7)) comparator_6 (
    .a(Instruction[6:0]), .b(7'b1101111), .eq(opcode_111));  // open: gt, lt
  Comparator #(.mode("unsigned"), .width(7)) comparator_7 (
    .a(Instruction[6:0]), .b(7'b0010111), .eq(opcode_23));  // open: gt, lt
  Comparator #(.mode("unsigned"), .width(7)) comparator_8 (
    .a(Instruction[6:0]), .b(7'b0110111), .eq(opcode_55));  // open: gt, lt
  Comparator #(.mode("unsigned"), .width(7)) comparator_9 (
    .a(Instruction[6:0]), .b(7'b1100111), .eq(opcode_103));  // open: gt, lt
  and and_7 (s_add, opcode_51, funct3_0, funct7_0);
  and and_8 (s_mul, opcode_51, funct3_0, funct7_1);
  and and_9 (s_sub, opcode_51, funct3_0, funct7_32);
  and and_10 (s_sll, opcode_51, funct3_1, funct7_0);
  and and_11 (s_mulh, opcode_51, funct3_1, funct7_1);
  and and_12 (s_mulhu, opcode_51, funct3_3, funct7_1);
  and and_13 (s_slt, opcode_51, funct3_2, funct7_0);
  and and_14 (s_xor, opcode_51, funct3_4, funct7_0);
  and and_15 (s_srl, opcode_51, funct3_5, funct7_0);
  and and_16 (s_sra, opcode_51, funct3_5, funct7_32);
  and and_17 (s_or, opcode_51, funct3_6, funct7_0);
  and and_18 (s_and, opcode_51, funct3_7, funct7_0);
  Comparator #(.mode("unsigned"), .width(3)) comparator_10 (
    .a(Instruction[14:12]), .b(3'b000), .eq(funct3_0));  // open: gt, lt
  Comparator #(.mode("unsigned"), .width(3)) comparator_11 (
    .a(Instruction[14:12]), .b(3'b001), .eq(funct3_1));  // open: gt, lt
  Comparator #(.mode("unsigned"), .width(3)) comparator_12 (
    .a(Instruction[14:12]), .b(3'b010), .eq(funct3_2));  // open: gt, lt
  Comparator #(.mode("unsigned"), .width(3)) comparator_13 (
    .a(Instruction[14:12]), .b(3'b011), .eq(funct3_3));  // open: gt, lt
  Comparator #(.mode("unsigned"), .width(3)) comparator_14 (
    .a(Instruction[14:12]), .b(3'b100), .eq(funct3_4));  // open: gt, lt
  Comparator #(.mode("unsigned"), .width(3)) comparator_15 (
    .a(Instruction[14:12]), .b(3'b101), .eq(funct3_5));  // open: gt, lt
  Comparator #(.mode("unsigned"), .width(3)) comparator_16 (
    .a(Instruction[14:12]), .b(3'b110), .eq(funct3_6));  // open: gt, lt
  Comparator #(.mode("unsigned"), .width(3)) comparator_17 (
    .a(Instruction[14:12]), .b(3'b111), .eq(funct3_7));  // open: gt, lt
  and and_19 (s_lb, opcode_3, funct3_0);
  and and_20 (s_lh, opcode_3, funct3_1);
  and and_21 (s_lw, opcode_3, funct3_2);
  Comparator #(.mode("unsigned"), .width(7)) comparator_18 (
    .a(Instruction[31:25]), .b({7{1'b0}}), .eq(funct7_0));  // open: gt, lt
  Comparator #(.mode("unsigned"), .width(7)) comparator_19 (
    .a(Instruction[31:25]), .b(7'b0000001), .eq(funct7_1));  // open: gt, lt
  Comparator #(.mode("unsigned"), .width(7)) comparator_20 (
    .a(Instruction[31:25]), .b(7'b0110010), .eq(funct7_32));  // open: gt, lt
  and and_22 (s_addi, opcode_19, funct3_0);
  and and_23 (s_slli, opcode_19, funct3_1, funct7_0);
  and and_24 (s_slti, opcode_19, funct3_2);
  and and_25 (s_xori, opcode_19, funct3_4);
  and and_26 (s_srli, opcode_19, funct3_5, funct7_0);
  and and_27 (s_srai, opcode_19, funct3_5, funct7_32);
  and and_28 (s_ori, opcode_19, funct3_6);
  and and_29 (s_andi, opcode_19, funct3_7);
  and and_30 (s_sb, opcode_35, funct3_0);
  and and_31 (s_sh, opcode_35, funct3_1);
  and and_32 (s_sw, opcode_35, funct3_2);
  and and_33 (s_beq, opcode_99, funct3_0);
  and and_34 (s_bne, opcode_99, funct3_1);
  and and_35 (s_blt, opcode_99, funct3_4);
  and and_36 (s_bge, opcode_99, funct3_5);
  and and_37 (s_bltu, opcode_99, funct3_6);
  and and_38 (s_bgeu, opcode_99, funct3_7);
  and and_39 (s_jalr, opcode_103, funct3_0);

  // Other names for the same wires on the sheet: opcode[6:0] = Instruction[6:0]; funct3[2:0] = Instruction[14:12];
  //   funct7[6:0] = Instruction[31:25]; s_auipc = opcode_23; s_jal = opcode_111; s_lui = opcode_55

  // Notes on the sheet:
  //   INPUTS to your circuit
  //   Connect ROM Input here ->
  //   contents of rom_1 (hex, n*v repeats v):
  //   1001 1401 1601 1081 1481 1581 1101 1201 1281 1681 1301 1381 41 41 41 1041 10c1 1141 1241 12c1 16c1
  //   1341 13c1 842 842 842 4*64 74 74 1067 17e7 2069 2041
  //   ROM FOR CONTROL LOGIC
  //   DON'T CHANGE THE LOCATIONS OF THE INPUTS AND OUTPUTS!
  //   This is only if you choose to do the ROM option
  //   OUTPUT from your circuit
  //   Reminder: If using ROM, use combinational logic for PCSel
endmodule
