// Logisim project partial-store.circ as structural Verilog: 1 circuit, main circuit partial_store
module partial_store (
  input  [31:0] Instruction,
  input  [31:0] MemAddress,
  input  [31:0] DataFromReg,
  input  MemWEn,
  output [3:0] MemWriteMask,
  output [31:0] DataToMem
);

  wire [3:0] sb_mask, sh_mask;
  wire [31:0] bit_extender_1_out, bit_extender_2_out, sb, sh;

  Multiplexer #(.select(3), .width(32)) multiplexer_1 (
    .in0(sb), .in1(sh), .in2(DataFromReg), .out(DataToMem), .sel(Instruction[14:12]), .en(MemWEn));  // open: in3, in4, in5, in6, in7
  Multiplexer #(.select(3), .width(4)) multiplexer_2 (
    .in0(sb_mask), .in1(sh_mask), .in2(4'b1111), .out(MemWriteMask), .sel(Instruction[14:12]), .en(MemWEn));  // open: in3, in4, in5, in6, in7
  assign bit_extender_1_out = {{24{1'b0}}, DataFromReg[7:0]};  // Bit_Extender bit_extender_1
  assign bit_extender_2_out = {{16{1'b0}}, DataFromReg[15:0]};  // Bit_Extender bit_extender_2
  Multiplexer #(.enable("false"), .select(2), .width(32)) multiplexer_3 (
    .in0(bit_extender_1_out),
    .in1({bit_extender_1_out[31:16], bit_extender_1_out[7:0], bit_extender_1_out[15:8]}),
    .in2({bit_extender_1_out[31:24], bit_extender_1_out[7:0], bit_extender_1_out[23:8]}),
    .in3({bit_extender_1_out[7:0], bit_extender_1_out[23:8], bit_extender_1_out[31:24]}), .out(sb),
    .sel(MemAddress[1:0]));
  Multiplexer #(.enable("false"), .select(2), .width(32)) multiplexer_4 (
    .in0(bit_extender_2_out), .in1({bit_extender_2_out[7:0], bit_extender_2_out[31:8]}),
    .in2({bit_extender_2_out[15:0], bit_extender_2_out[31:16]}), .out(sh), .sel(MemAddress[1:0]));  // open: in3
  Multiplexer #(.enable("false"), .select(2), .width(4)) multiplexer_5 (
    .in0(4'b0001), .in1(4'b0010), .in2(4'b0100), .in3(4'b1000), .out(sb_mask), .sel(MemAddress[1:0]));
  Multiplexer #(.enable("false"), .select(2), .width(4)) multiplexer_6 (
    .in0(4'b0011), .in1(4'b0110), .in2(4'b1100), .out(sh_mask), .sel(MemAddress[1:0]));  // open: in3

  // Other names for the same wires on the sheet: sw[31:0] = DataFromReg

  // Notes on the sheet:
  //   INPUTS to your circuit
  //   DON'T CHANGE THE LOCATIONS OF THE INPUTS AND OUTPUTS!
  //   OUTPUT from your circuit
endmodule
