// Logisim project regfile.circ as structural Verilog: 1 circuit, main circuit regfile
module regfile (
  input  [4:0] ReadReg1,
  input  [4:0] ReadReg2,
  input  [4:0] WriteReg,
  input  [31:0] RegWriteData,
  input  RegWEn,
  input  clk,
  output [31:0] ra,
  output [31:0] sp,
  output [31:0] t0,
  output [31:0] t1,
  output [31:0] t2,
  output [31:0] s0,
  output [31:0] s1,
  output [31:0] a0,
  output [31:0] RegReadData1,
  output [31:0] RegReadData2
);

  wire RegWE1, RegWE2, RegWE3, RegWE4, RegWE5, RegWE6, RegWE7, RegWE8, RegWE9, RegWE10, RegWE11, RegWE12,
       RegWE13, RegWE14, RegWE15, RegWE16, RegWE17, RegWE18, RegWE19, RegWE20, RegWE21, RegWE22, RegWE23,
       RegWE24, RegWE25, RegWE26, RegWE27, RegWE28, RegWE29, RegWE30, RegWE31;
  wire [31:0] a1, a2, a3, a4, a5, a6, a7, gp, s2, s3, s4, s5, s6, s7, s8, s9, s10, s11, t3, t4, t5, t6, tp,
       zero;

  Demultiplexer #(.enable("false"), .select(5)) demultiplexer_1 (
    .out1(RegWE1), .out2(RegWE2), .out3(RegWE3), .out4(RegWE4), .out5(RegWE5), .out6(RegWE6), .out7(RegWE7),
    .out8(RegWE8), .out9(RegWE9), .out10(RegWE10), .out11(RegWE11), .out12(RegWE12), .out13(RegWE13),
    .out14(RegWE14), .out15(RegWE15), .out16(RegWE16), .out17(RegWE17), .out18(RegWE18), .out19(RegWE19),
    .out20(RegWE20), .out21(RegWE21), .out22(RegWE22), .out23(RegWE23), .out24(RegWE24), .out25(RegWE25),
    .out26(RegWE26), .out27(RegWE27), .out28(RegWE28), .out29(RegWE29), .out30(RegWE30), .out31(RegWE31),
    .in(RegWEn), .sel(WriteReg));  // open: out0
  Register #(.width(32)) register_1 (.D(RegWriteData), .en(RegWE1), .clk(clk), .Q(ra));  // open: clr
  Register #(.width(32)) register_2 (.D(RegWriteData), .en(RegWE4), .clk(clk), .Q(tp));  // open: clr
  Register #(.width(32)) register_3 (.D(RegWriteData), .en(RegWE7), .clk(clk), .Q(t2));  // open: clr
  Register #(.width(32)) register_4 (.D(RegWriteData), .en(RegWE10), .clk(clk), .Q(a0));  // open: clr
  Register #(.width(32)) register_5 (.D(RegWriteData), .en(RegWE13), .clk(clk), .Q(a3));  // open: clr
  Register #(.width(32)) register_6 (.D(RegWriteData), .en(RegWE16), .clk(clk), .Q(a6));  // open: clr
  Register #(.width(32)) register_7 (.D(RegWriteData), .en(RegWE19), .clk(clk), .Q(s3));  // open: clr
  Register #(.width(32)) register_8 (.D(RegWriteData), .en(RegWE22), .clk(clk), .Q(s6));  // open: clr
  Register #(.width(32)) register_9 (.D(RegWriteData), .en(RegWE25), .clk(clk), .Q(s9));  // open: clr
  Register #(.width(32)) register_10 (.D(RegWriteData), .en(RegWE28), .clk(clk), .Q(t3));  // open: clr
  Register #(.width(32)) register_11 (.D(RegWriteData), .en(RegWE31), .clk(clk), .Q(t6));  // open: clr
  Register #(.width(32)) register_12 (.D(RegWriteData), .en(RegWE2), .clk(clk), .Q(sp));  // open: clr
  Register #(.width(32)) register_13 (.D(RegWriteData), .en(RegWE5), .clk(clk), .Q(t0));  // open: clr
  Register #(.width(32)) register_14 (.D(RegWriteData), .en(RegWE8), .clk(clk), .Q(s0));  // open: clr
  Register #(.width(32)) register_15 (.D(RegWriteData), .en(RegWE11), .clk(clk), .Q(a1));  // open: clr
  Register #(.width(32)) register_16 (.D(RegWriteData), .en(RegWE14), .clk(clk), .Q(a4));  // open: clr
  Register #(.width(32)) register_17 (.D(RegWriteData), .en(RegWE17), .clk(clk), .Q(a7));  // open: clr
  Register #(.width(32)) register_18 (.D(RegWriteData), .en(RegWE20), .clk(clk), .Q(s4));  // open: clr
  Register #(.width(32)) register_19 (.D(RegWriteData), .en(RegWE23), .clk(clk), .Q(s7));  // open: clr
  Register #(.width(32)) register_20 (.D(RegWriteData), .en(RegWE26), .clk(clk), .Q(s10));  // open: clr
  Register #(.width(32)) register_21 (.D(RegWriteData), .en(RegWE29), .clk(clk), .Q(t4));  // open: clr
  Register #(.width(32)) register_22 (.D(RegWriteData), .en(1'b0), .clk(clk), .Q(zero));  // open: clr
  Register #(.width(32)) register_23 (.D(RegWriteData), .en(RegWE3), .clk(clk), .Q(gp));  // open: clr
  Register #(.width(32)) register_24 (.D(RegWriteData), .en(RegWE6), .clk(clk), .Q(t1));  // open: clr
  Register #(.width(32)) register_25 (.D(RegWriteData), .en(RegWE9), .clk(clk), .Q(s1));  // open: clr
  Register #(.width(32)) register_26 (.D(RegWriteData), .en(RegWE12), .clk(clk), .Q(a2));  // open: clr
  Register #(.width(32)) register_27 (.D(RegWriteData), .en(RegWE15), .clk(clk), .Q(a5));  // open: clr
  Register #(.width(32)) register_28 (.D(RegWriteData), .en(RegWE18), .clk(clk), .Q(s2));  // open: clr
  Register #(.width(32)) register_29 (.D(RegWriteData), .en(RegWE21), .clk(clk), .Q(s5));  // open: clr
  Register #(.width(32)) register_30 (.D(RegWriteData), .en(RegWE24), .clk(clk), .Q(s8));  // open: clr
  Register #(.width(32)) register_31 (.D(RegWriteData), .en(RegWE27), .clk(clk), .Q(s11));  // open: clr
  Register #(.width(32)) register_32 (.D(RegWriteData), .en(RegWE30), .clk(clk), .Q(t5));  // open: clr
  Multiplexer #(.enable("false"), .select(5), .width(32)) multiplexer_1 (
    .in0(zero), .in1(ra), .in2(sp), .in3(gp), .in4(tp), .in5(t0), .in6(t1), .in7(t2), .in8(s0), .in9(s1),
    .in10(a0), .in11(a1), .in12(a2), .in13(a3), .in14(a4), .in15(a5), .in16(a6), .in17(a7), .in18(s2),
    .in19(s3), .in20(s4), .in21(s5), .in22(s6), .in23(s7), .in24(s8), .in25(s9), .in26(s10), .in27(s11),
    .in28(t3), .in29(t4), .in30(t5), .in31(t6), .out(RegReadData1), .sel(ReadReg1));
  Multiplexer #(.enable("false"), .select(5), .width(32)) multiplexer_2 (
    .in0(zero), .in1(ra), .in2(sp), .in3(gp), .in4(tp), .in5(t0), .in6(t1), .in7(t2), .in8(s0), .in9(s1),
    .in10(a0), .in11(a1), .in12(a2), .in13(a3), .in14(a4), .in15(a5), .in16(a6), .in17(a7), .in18(s2),
    .in19(s3), .in20(s4), .in21(s5), .in22(s6), .in23(s7), .in24(s8), .in25(s9), .in26(s10), .in27(s11),
    .in28(t3), .in29(t4), .in30(t5), .in31(t6), .out(RegReadData2), .sel(ReadReg2));

  // Notes on the sheet:
  //   INPUTS to your circuit
  //   DON'T CHANGE THE LOCATIONS OF THE INPUTS AND OUTPUTS!
  //   These are DEBUG/TEST outputs from your circuit.
  //   OUTPUTS from your circuit
endmodule
